# Fritzing sketch Schematics (saved by Fritzing 0.9.3b)

parts:
  Part1 = Arduino Uno (Rev3)  # not connected
  Part2 = Dragino LoRa Shield V1.4
  hc-sr1 = hc-sr04

nets:
  N1: Part2.4, hc-sr1.Echo
  N2: Part2.3, hc-sr1.Trig
  5V: Part2.5V, hc-sr1.VCC
  GND: Part2.GND, hc-sr1.GND
